# Fritzing sketch nfc_servo (saved by Fritzing 0.8.7b)
circuit board: 8.46667cm x 5.64444cm
breadboards: 1

parts:
  ARDUINO_UNO = Arduino Uno (Rev3)
  J1_Servo = Basic Servo
  C1_1uF = Electrolytic Capacitor [capacitance=1µF voltage=50V package="100 mil [THT, electrolytic]"]
  C2_100nF = Tantalum Capacitor [capacitance=100nF package="100 mil [THT, tantalum]"]
  U1_L7807 = Voltage Regulator - 5V [package="DPak [SMD]"]
  RFID-RC522 = RFID-RC522-v2

nets:
  N1: ARDUINO_UNO.D9_PWM, RFID-RC522.RST
  N2: ARDUINO_UNO.D10_PWM/SS, RFID-RC522.SDA
  N3: ARDUINO_UNO.D11_PWM/MOSI, RFID-RC522.MOSI
  N4: ARDUINO_UNO.D12/MISO, RFID-RC522.MISO
  N5: ARDUINO_UNO.D13/SCK, RFID-RC522.SCK
  GND: ARDUINO_UNO.GND, RFID-RC522.GND
  N6: ARDUINO_UNO.D3_PWM, J1_Servo.vcc
  3V3: ARDUINO_UNO.3V3, RFID-RC522.3.3V
  N7: ARDUINO_UNO.VIN, C2_100nF.+, U1_L7807.input_voltage
  GND_2: J1_Servo.gnd, C1_1uF.-, C2_100nF.-, U1_L7807.GND
  N8: J1_Servo.pulse, C1_1uF.+, U1_L7807.output_voltage

notes:
  [ EXIT ROOM ]

custom parts:
  RFID-RC522-v2: A simple China made RFID-RC522 Reader; do check the pin labels, as this is a MFRC522 based clone.
